// Logisim project cpu.circ as structural Verilog: 1 circuit, main circuit main
module main (
);

  wire ACC_WRITE, ALU_CARRY, ALU_MODE, ALU_S0, ALU_S1, ALU_S2, ALU_S3, and_1_out, and_2_out, and_3_out,
       and_4_out, B_WRITE, button_1_out, button_2_out, button_3_out, C_WRITE, CARRY_SYS, CARRY_USR, CLK,
       clock_1_out, d_ff_1_q, D_WRITE, E_WRITE, END_INSTR, EQUAL_SYS, EQUAL_USR, FLAGS_SYS_UPDATE,
       FLAGS_USR_UPDATE, HALT, IR_WRITE, l_74181_cab58b94_1_p16, l_74181_cab58b94_2_p2,
       l_74181_cab58b94_2_p20, nACC_OUT, nAH_OUT, nAL_OUT, nALU_OUT, nBC_OUT, nDE_OUT, not_1_out, not_2_out,
       not_3_out, not_4_out, not_5_out, not_6_out, not_7_out, not_8_out, not_9_out, nPC_OUT, nRAM_OUT,
       nRAM_WRITE, nSP_OUT, nTMP_OUT, or_1_out, PC_H_WRITE, PC_L_WRITE, RST, SP_H_WRITE, SP_L_WRITE,
       TMP_WRITE;
  wire [1:0] l_74181_cab58b94_1_p13;
  wire [3:0] counter_1_q;
  wire [6:0] keyboard_1_data;
  wire [7:0] ACC_q, B_q, C_q, controlled_buffer_5_out, D_q, E_q, l_74181_cab58b94_2_p22, PC_H_q, PC_L_q,
       ram_1_data, register_1_q, SP_H_q, SP_L_q, TMP_q;
  wire [15:0] controlled_buffer_1_out;
  wire [30:30] rom_1_data;

  // Probe on l_74181_cab58b94_2_p22
  Register PC_H (.D(l_74181_cab58b94_2_p22), .en(PC_H_WRITE), .clk(CLK), .Q(PC_H_q), .clr(RST));
  Register PC_L (.D(l_74181_cab58b94_2_p22), .en(PC_L_WRITE), .clk(CLK), .Q(PC_L_q), .clr(RST));
  Register SP_H (.D(l_74181_cab58b94_2_p22), .en(SP_H_WRITE), .clk(CLK), .Q(SP_H_q), .clr(RST));
  Register SP_L (.D(l_74181_cab58b94_2_p22), .en(SP_L_WRITE), .clk(CLK), .Q(SP_L_q), .clr(RST));
  Register B (.D(l_74181_cab58b94_2_p22), .en(B_WRITE), .clk(CLK), .Q(B_q), .clr(RST));
  Register C (.D(l_74181_cab58b94_2_p22), .en(C_WRITE), .clk(CLK), .Q(C_q), .clr(RST));
  Register D (.D(l_74181_cab58b94_2_p22), .en(D_WRITE), .clk(CLK), .Q(D_q), .clr(RST));
  Register E (.D(l_74181_cab58b94_2_p22), .en(E_WRITE), .clk(CLK), .Q(E_q), .clr(RST));
  assign controlled_buffer_1_out = not_1_out ? {PC_H_q, PC_L_q} : 16'bz;  // Controlled_Buffer controlled_buffer_1
  not not_1 (not_1_out, nPC_OUT);
  assign controlled_buffer_1_out = not_2_out ? {SP_H_q, SP_L_q} : 16'bz;  // Controlled_Buffer controlled_buffer_2
  not not_2 (not_2_out, nSP_OUT);
  assign controlled_buffer_1_out = not_3_out ? {B_q, C_q} : 16'bz;  // Controlled_Buffer controlled_buffer_3
  not not_3 (not_3_out, nBC_OUT);
  assign controlled_buffer_1_out = not_4_out ? {D_q, E_q} : 16'bz;  // Controlled_Buffer controlled_buffer_4
  not not_4 (not_4_out, nDE_OUT);
  // Probe on controlled_buffer_1_out
  Pull_Resistor pull_resistor_1 (.node(controlled_buffer_1_out));
  not not_5 (not_5_out, nAH_OUT);
  assign controlled_buffer_5_out = not_5_out ? controlled_buffer_1_out[15:8] : 8'bz;  // Controlled_Buffer controlled_buffer_5
  assign controlled_buffer_5_out = not_6_out ? controlled_buffer_1_out[7:0] : 8'bz;  // Controlled_Buffer controlled_buffer_6
  not not_6 (not_6_out, nAL_OUT);
  Button button_1 (.out(button_1_out));
  Button button_2 (.out(button_2_out));
  RAM #(.addrWidth(15), .asyncread("true"), .databus("bidir"), .\type ("nonvolatile")) ram_1 (
    .addr(controlled_buffer_1_out[14:0]), .we(and_1_out), .oe(and_2_out), .clk(CLK), .data(ram_1_data));
  and and_1 (and_1_out, ~controlled_buffer_1_out[15], ~nRAM_WRITE);  // AND_Gate
  and and_2 (and_2_out, ~controlled_buffer_1_out[15], ~nRAM_OUT);  // AND_Gate
  TTY tty_1 (.data(ram_1_data[6:0]), .clk(CLK), .we(and_3_out), .clr(RST));
  and and_3 (and_3_out, controlled_buffer_1_out[15], ~nRAM_WRITE);  // AND_Gate
  and and_4 (and_4_out, controlled_buffer_1_out[15], ~nRAM_OUT);  // AND_Gate
  D_Flip_Flop d_ff_1 (.D(1'b0), .clk(HALT), .Q(d_ff_1_q), .preset(button_1_out), .reset(button_2_out));  // open: Qn
  Keyboard keyboard_1 (.clk(CLK), .re(and_4_out), .clr(RST), .data(keyboard_1_data));  // open: avail
  Clock clock_1 (.out(clock_1_out));
  Button button_3 (.out(button_3_out));
  and and_5 (CLK, d_ff_1_q, clock_1_out);
  and and_6 (RST, ~clock_1_out, button_3_out);  // AND_Gate
  assign ram_1_data = and_4_out ? {1'b0, keyboard_1_data} : 8'bz;  // Controlled_Buffer controlled_buffer_7
  not not_7 (not_7_out, nALU_OUT);
  assign ram_1_data = not_7_out ? l_74181_cab58b94_2_p22 : 8'bz;  // Controlled_Buffer controlled_buffer_8
  // Probe on ram_1_data
  Pull_Resistor pull_resistor_2 (.node(ram_1_data));
  Register register_1 (.D(ram_1_data), .en(IR_WRITE), .clk(CLK), .Q(register_1_q), .clr(RST));
  // Probe on l_74181_cab58b94_2_p22
  Counter #(.max('hf), .width(4)) counter_1 (
    .count(1'b1), .Q(counter_1_q), .clk(CLK), .clr(or_1_out));  // open: load, D, carry, up
  or or_1 (or_1_out, END_INSTR, RST);
  Register ACC (.D(l_74181_cab58b94_2_p22), .en(ACC_WRITE), .clk(CLK), .Q(ACC_q), .clr(RST));
  Register TMP (.D(l_74181_cab58b94_2_p22), .en(TMP_WRITE), .clk(CLK), .Q(TMP_q), .clr(RST));
  ROM #(.addrWidth(16), .dataWidth(32)) rom_1 (
    .addr({CARRY_USR, EQUAL_USR, CARRY_SYS, EQUAL_SYS, register_1_q, counter_1_q}),
    .data({END_INSTR, rom_1_data[30], TMP_WRITE, ACC_WRITE, nTMP_OUT, nACC_OUT, FLAGS_SYS_UPDATE, FLAGS_USR_UPDATE, ALU_CARRY, ALU_MODE, ALU_S3, ALU_S2, ALU_S1, ALU_S0, nRAM_WRITE, IR_WRITE, E_WRITE, D_WRITE, C_WRITE, B_WRITE, SP_L_WRITE, SP_H_WRITE, PC_L_WRITE, PC_H_WRITE, nRAM_OUT, nAH_OUT, nAL_OUT, nALU_OUT, nDE_OUT, nBC_OUT, nSP_OUT, nPC_OUT}));
  assign controlled_buffer_5_out = not_8_out ? ACC_q : 8'bz;  // Controlled_Buffer controlled_buffer_9
  not not_8 (not_8_out, nACC_OUT);
  Pull_Resistor pull_resistor_3 (.node(controlled_buffer_5_out));
  assign ram_1_data = not_9_out ? TMP_q : 8'bz;  // Controlled_Buffer controlled_buffer_10
  not not_9 (not_9_out, nTMP_OUT);
  Pull_Resistor pull_resistor_4 (.node(ram_1_data));
  // Probe on controlled_buffer_5_out
  // Probe on ram_1_data
  // L_74181_cab58b94 l_74181_cab58b94_1: pin names not known; wires that end beside it: ALU_S3, ALU_S2, ALU_S1, ALU_S0, ram_1_data[7], controlled_buffer_5_out[7], ram_1_data[6], controlled_buffer_5_out[6], ram_1_data[5], controlled_buffer_5_out[5], ram_1_data[4], controlled_buffer_5_out[4], l_74181_cab58b94_1_p13[0], l_74181_cab58b94_2_p22[7], l_74181_cab58b94_2_p22[6], l_74181_cab58b94_1_p16, l_74181_cab58b94_2_p22[5], l_74181_cab58b94_2_p22[4]
  // L_74181_cab58b94 l_74181_cab58b94_2: pin names not known; wires that end beside it: ALU_MODE, l_74181_cab58b94_2_p2, ALU_S3, ALU_S2, ALU_S1, ALU_S0, ram_1_data[3], controlled_buffer_5_out[3], ram_1_data[2], controlled_buffer_5_out[2], ram_1_data[1], controlled_buffer_5_out[1], ram_1_data[0], controlled_buffer_5_out[0], ALU_MODE, ALU_CARRY, l_74181_cab58b94_2_p2, l_74181_cab58b94_2_p22[3], l_74181_cab58b94_2_p22[2], l_74181_cab58b94_2_p20, l_74181_cab58b94_2_p22[1], l_74181_cab58b94_2_p22[0]
  and and_7 (l_74181_cab58b94_1_p13[1], l_74181_cab58b94_1_p16, l_74181_cab58b94_2_p20);
  Register #(.width(2)) register_2 (
    .D(l_74181_cab58b94_1_p13), .en(FLAGS_USR_UPDATE), .clk(CLK), .Q({EQUAL_USR, CARRY_USR}), .clr(RST));
  Register #(.width(2)) register_3 (
    .D(l_74181_cab58b94_1_p13), .en(FLAGS_SYS_UPDATE), .clk(CLK), .Q({EQUAL_SYS, CARRY_SYS}), .clr(RST));

  // Notes on the sheet:
  //   contents of rom_1 (hex, n*v repeats v):
  //   e03025e c0201be 14*8c0200ff e03025e c0201be 1c6a007e e0202de c0201be 11*8c0200ff e03025e c0201be
  //   c6a107e e0202de c0201be 11*8c0200ff e03025e c0201be c6a207e e0202de c0201be 11*8c0200ff e03025e
  //   c0201be c6a407e e0202de c0201be 11*8c0200ff e03025e c0201be c6a807e e0202de c0201be 11*8c0200ff
  //   e03025e c0201be c6a107e e0202de c0201be c6a207e e0202de c0201be 8*8c0200ff e03025e c0201be c6a407e
  //   e0202de c0201be c6a807e e0202de c0201be 8*8c0200ff e03025e c0201be c6a047e e0202de c0201be c6a087e
  //   e0202de c0201be 8*8c0200ff e03025e c0201be 19a6007e e0202de c0201be 11*8c0200ff e03025e c0201be
  //   191a007e e0202de c0201be 11*8c0200ff e03025e c0201be 186e007e e0202de c0201be 11*8c0200ff e03025e
  //   c0201be 14*8c0200ff e03025e c0201be 14*8c0200ff e03025e c0201be 14*8c0200ff e03025e c0201be
  //   14*8c0200ff e03025e c0201be 2c8200bb 11a600ff 12*8c0200ff e03025e c0201be 2c8200bb 111a00ff
  //   12*8c0200ff e03025e c0201be 14*8c0200ff e03025e c0201be 14*8c0200ff e03025e c0201be 14*8c0200ff
  //   e03025e c0201be 14*8c0200ff e03025e c0201be 14*8c0200ff e03025e c0201be 14*8c0200ff e03025e c0201be
  //   14*8c0200ff e03025e c0201be 14*8c0200ff e03025e c0201be 14*8c0200ff e03025e c0201be 14*8c0200ff
  //   e03025e c0201be 14*8c0200ff e03025e c0201be 14*8c0200ff e03025e c0201be 14*8c0200ff e03025e c0201be
  //   14*8c0200ff e03025e c0201be 14*8c0200ff e03025e c0201be 14*8c0200ff e03025e c0201be 14*8c0200ff
  //   e03025e c0201be 14*8c0200ff e03025e c0201be 14*8c0200ff e03025e c0201be 14*8c0200ff e03025e c0201be
  //   14*8c0200ff e03025e c0201be 14*8c0200ff e03025e c0201be 14*8c0200ff e03025e c0201be 14*8c0200ff
  //   e03025e c0201be 14*8c0200ff e03025e c0201be 14*8c0200ff e03025e c0201be 19a6007b 13*8c0200ff e03025e
  //   c0201be 14*8c0200ff e03025e c0201be 14*8c0200ff e03025e c0201be 14*8c0200ff e03025e c0201be
  //   14*8c0200ff e03025e c0201be 14*8c0200ff e03025e c0201be 14*8c0200ff e03025e c0201be 14*8c0200ff
  //   e03025e c0201be 14*8c0200ff e03025e c0201be 14*8c0200ff e03025e c0201be 14*8c0200ff e03025e c0201be
  //   14*8c0200ff e03025e c0201be 14*8c0200ff e03025e c0201be 14*8c0200ff e03025e c0201be 14*8c0200ff
  //   e03025e c0201be ebe08dd c8204bd 88000ed 11*8c0200ff e03025e c0201be ebe08dd c8204bd 2c8200bb 40000fd
  //   10*8c0200ff e03025e c0201be ebe08dd c8204bd 2c8200db 40000fd 10*8c0200ff e03025e c0201be ebe08dd
  //   c8204bd 2c8200b7 40000fd 10*8c0200ff e03025e c0201be ebe08dd c8204bd 2c8200d7 40000fd 10*8c0200ff
  //   e03025e c0201be 1c6a007d e0208dd c0204bd 11*8c0200ff e03025e c0201be c6a107d e0208dd c0204bd
  //   11*8c0200ff e03025e c0201be c6a207d e0208dd c0204bd 11*8c0200ff e03025e c0201be c6a407d e0208dd
  //   c0204bd 11*8c0200ff e03025e c0201be c6a807d e0208dd c0204bd 11*8c0200ff e03025e c0201be ebe08dd
  //   c8204bd 2c8200db 40000fd ebe08dd c8204bd 2c8200bb 40000fd 6*8c0200ff e03025e c0201be ebe08dd c8204bd
  //   2c8200d7 40000fd ebe08dd c8204bd 2c8200b7 40000fd 6*8c0200ff e03025e c0201be c6a107d e0208dd c0204bd
  //   c6a207d e0208dd c0204bd 8*8c0200ff e03025e c0201be c6a407d e0208dd c0204bd c6a807d e0208dd c0204bd
  //   8*8c0200ff e03025e c0201be e0220db c0210bb 12*8c0200ff e03025e c0201be e0280d7 c0240b7 12*8c0200ff
  //   e03025e c0201be ebe20db c8210bb 12*8c0200ff e03025e c0201be ebe80db c8240bb 12*8c0200ff e03025e
  //   c0201be 2c6a007e e0202de c0201be c6a027e 46a01ff 9*8c0200ff e03025e c0201be 14*8c0200ff e03025e
  //   c0201be 14*8c0200ff e03025e c0201be 14*8c0200ff e03025e c0201be 14*8c0200ff e03025e c0201be 2c6a007e
  //   e0202de c0201be c6a027e 46a01ff 9*8c0200ff e03025e c0201be 14*8c0200ff e03025e c0201be 14*8c0200ff
  //   e03025e c0201be 14*8c0200ff e03025e c0201be 14*8c0200ff e03025e c0201be 2c6a007e e0202de c0201be
  //   e0202de c0201be 9*8c0200ff e03025e c0201be 14*8c0200ff e03025e c0201be 14*8c0200ff e03025e c0201be
  //   14*8c0200ff e03025e c0201be 14*8c0200ff e03025e c0201be 2c6a007e e0202de c0201be e0202de c0201be
  //   9*8c0200ff e03025e c0201be 14*8c0200ff e03025e c0201be 14*8c0200ff e03025e c0201be 14*8c0200ff
  //   e03025e c0201be 14*8c0200ff e03025e c0201be 2c6a007e e0202de c0201be c6a027e 46a01ff 9*8c0200ff
  //   e03025e c0201be 14*8c0200ff e03025e c0201be 14*8c0200ff e03025e c0201be 14*8c0200ff e03025e c0201be
  //   14*8c0200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
endmodule
